// Logisim project CPU.circ as structural Verilog: 1 circuit, main circuit main
module main (
  input  in_1,
  input  in_2,
  input  in_3,
  input  in_4,
  input  in_5,
  input  in_6,
  input  in_7,
  input  in_8,
  input  in_9,
  input  in_10,
  input  in_11,
  input  in_12,
  input  in_13,
  input  in_14,
  input  in_15,
  input  in_16,
  input  in_17,
  input  in_18,
  input  in_19,
  input  in_20,
  input  in_21,
  input  in_22,
  input  in_23,
  input  in_24,
  input  in_25,
  input  in_26,
  input  in_27,
  input  in_28,
  input  in_29,
  input  in_30,
  input  in_31,
  input  in_32,
  input  in_33,
  input  in_34,
  input  in_35,
  input  in_36,
  input  in_37,
  input  in_38,
  input  [2:0] in_39,
  input  in_40,
  input  in_41
);

  wire Clk, MAR_p7, or_1_out;
  wire [3:0] alu_1_flags, undriven;
  wire [7:0] ACC_dout, alu_1_result, Flags_dout, lTMP_dout, pull_resistor_1_node, RA_dout, RB_dout, RC_dout,
       RD_dout, Tmp_dout;
  wire [7:4] undriven_2;
  wire [15:0] Addr, PC_p7, SP_p7;

  Clock clock_1 (.out(Clk));
  _8bitReg lTMP (
    .Load(in_7), .Din(pull_resistor_1_node), .nCarryIn(1'b1), .Reset(in_3), .Dout(lTMP_dout));  // open: Up_nDown, Clk
  // Probe on lTMP_dout
  Pull_Resistor pull_resistor_1 (.node(pull_resistor_1_node));
  assign Addr[7:0] = in_5 ? lTMP_dout : 8'bz;  // Controlled_Buffer controlled_buffer_1
  Pull_Resistor pull_resistor_2 (.node(Addr[7:0]));
  _8bitReg RA (
    .Up_nDown(in_6), .Load(in_2), .Din(pull_resistor_1_node), .Clk(Clk), .nCarryIn(in_4), .Reset(in_3),
    .Dout(RA_dout));
  // Probe on RA_dout
  // Probe on SP_p7
  // _16bitReg SP: pin names not known; wires that end beside it: in_15, in_11, Addr, in_13, Clk, in_3, SP_p7
  assign pull_resistor_1_node = in_1 ? RA_dout : 8'bz;  // Controlled_Buffer controlled_buffer_2
  assign Addr = in_9 ? SP_p7 : 16'bz;  // Controlled_Buffer controlled_buffer_3
  _8bitReg RB (
    .Up_nDown(in_14), .Load(in_10), .Din(pull_resistor_1_node), .Clk(Clk), .nCarryIn(in_12), .Reset(in_3),
    .Dout(RB_dout));
  // Probe on RB_dout
  // Probe on Addr
  assign Addr[15:8] = in_29 ? pull_resistor_1_node : 8'bz;  // Controlled_Buffer controlled_buffer_4
  assign pull_resistor_1_node = in_31 ? Addr[15:8] : 8'bz;  // Controlled_Buffer controlled_buffer_5
  assign pull_resistor_1_node = in_8 ? RB_dout : 8'bz;  // Controlled_Buffer controlled_buffer_6
  _8bitReg RC (
    .Up_nDown(in_22), .Load(in_18), .Din(pull_resistor_1_node), .Clk(Clk), .nCarryIn(in_20), .Reset(in_3),
    .Dout(RC_dout));
  // Probe on RC_dout
  // Probe on PC_p7
  // _16bitReg PC: pin names not known; wires that end beside it: in_23, in_19, Addr, in_21, Clk, in_3, PC_p7
  assign pull_resistor_1_node = in_16 ? RC_dout : 8'bz;  // Controlled_Buffer controlled_buffer_7
  assign Addr[7:0] = in_25 ? pull_resistor_1_node : 8'bz;  // Controlled_Buffer controlled_buffer_8
  assign Addr = in_17 ? PC_p7 : 16'bz;  // Controlled_Buffer controlled_buffer_9
  _8bitReg RD (.Up_nDown(in_30), .Load(in_26), .Clk(Clk), .nCarryIn(in_28), .Reset(in_3), .Dout(RD_dout));  // open: Din
  // Probe on RD_dout
  assign pull_resistor_1_node = in_27 ? Addr[7:0] : 8'bz;  // Controlled_Buffer controlled_buffer_10
  Pull_Resistor pull_resistor_3 (.node(Addr[15:8]));
  // Probe on pull_resistor_1_node
  assign pull_resistor_1_node = in_24 ? RD_dout : 8'bz;  // Controlled_Buffer controlled_buffer_11
  _8bitReg Tmp (
    .Load(in_38), .Din(pull_resistor_1_node), .nCarryIn(1'b1), .Reset(in_3), .Dout(Tmp_dout));  // open: Up_nDown, Clk
  // Probe on Tmp_dout
  ALU alu_1 (
    .Cin(Flags_dout[0]), .A(pull_resistor_1_node), .B(Tmp_dout), .Operation(in_39), .Flags(alu_1_flags),
    .Result(alu_1_result));
  // Probe on MAR_p7
  // _16bitReg MAR: pin names not known; wires that end beside it: in_37, in_33, Addr, in_35, Clk, in_3, MAR_p7
  _8bitReg Flags (
    .Load(in_34), .Din({undriven, alu_1_flags}), .nCarryIn(1'b1), .Reset(or_1_out), .Dout(Flags_dout));  // open: Up_nDown, Clk
  _8bitReg ACC (
    .Load(in_40), .Din(alu_1_result), .nCarryIn(1'b1), .Reset(in_3), .Dout(ACC_dout));  // open: Up_nDown, Clk
  // Probe on ACC_dout
  or or_1 (or_1_out, in_36, in_3);
  assign pull_resistor_1_node = in_41 ? ACC_dout : 8'bz;  // Controlled_Buffer controlled_buffer_12
  assign pull_resistor_1_node = in_32 ? {undriven_2, Flags_dout[3:0]} : 8'bz;  // Controlled_Buffer controlled_buffer_13

  // Other names for the same wires on the sheet: ACCena = in_41; ACCload = in_40; AhD = in_31; AlD = in_27;
  //   ALUop[2:0] = in_39; DAh = in_29; DAl = in_25; Fclr = in_36; Fena = in_32; Fload = in_34; lTMPena = in_5;
  //   lTMPload = in_7; MAR_nCarry = in_35; MARload = in_33; MARu_nd = in_37; PC_nCarry = in_21; PCena = in_17;
  //   PCload = in_19; PCu_nd = in_23; RA_nCarry = in_4; RAena = in_1; RAload = in_2; RAu_nd = in_6; RB_nCarry = in_12;
  //   RBena = in_8; RBload = in_10; RBu_nd = in_14; RC_nCarry = in_20; RCena = in_16; RCload = in_18; RCu_nd = in_22;
  //   RD_nCarry = in_28; RDena = in_24; RDload = in_26; RDu_nd = in_30; Rst = in_3; SP_nCarry = in_13; SPena = in_9;
  //   SPload = in_11; SPu_nd = in_15; TMPload = in_38
endmodule
